# Fritzing sketch FireSystemConnections (saved by Fritzing 1.0.6)
breadboards: 1

parts:
  Mod1 = Amica NodeMCU DEVKIT 1.0
  Part1 = Arduino Uno (Rev3)
  Water_Pump = DC Motor [voltage_(max)=6V voltage_(min)=3V]
  Alarm = Piezo Speaker
  Relay = 2 channel relay module [package=THT]
  J3 = Basic Servo
  12V = 4 x AAA Battery Mount [internal_resistance=0.1Ω]
  Mod2 = MQ-7 breakout
  C1 = Electrolytic Capacitor [capacitance=1mF voltage=16V package="100 mil [THT, electrolytic]"]
  J4 = Basic Servo
  C2 = Electrolytic Capacitor [capacitance=1mF voltage=16V package="100 mil [THT, electrolytic]"]
  S1 = KY-026
  S2 = KY-026
  A1 = DHT22 module

nets:
  N1: Mod1.pin1, Mod1.pin_10, Mod1.pin_26
  GND: Mod1.pin2, Mod1.pin_9, Mod1.pin_25, Mod1.pin_29, Part1.GND, Relay.pin_14, J3.gnd, Mod2.GND, C1.-, J4.gnd, C2.-, S1.pin2, S2.pin2, A1.-
  N2: Mod1.pin_13, Part1.A5/SCL
  N3: Mod1.pin_14, Part1.A4/SDA
  5V: Mod1.pin_30, Part1.5V, Relay.pin_13, J3.vcc, Mod2.VCC, C1.+, J4.vcc, C2.+, S1.pin3, S2.pin3, A1.+
  N4: Part1.A0, Mod2.AO
  N5: Part1.A1, A1.Out
  N6: Part1.A2, S1.pin1
  N7: Part1.A3, S2.pin1
  N8: Part1.D9_PWM, J3.pulse
  N9: Part1.D10_PWM/SS, J4.pulse
  N10: Part1.D12/MISO, Relay.pin_15
  N11: Part1.D13/SCK, Relay.pin_16
  N12: Water_Pump.pin_1, Relay.pin_4
  N13: Water_Pump.pin_2, Alarm.pin1, 12V.-
  N14: Alarm.pin2, Relay.pin_1
  N15: Relay.pin_2, Relay.pin_5, 12V.+

notes:
  Arduino <-> ESP
  I2C Communication
  PIN A4/A5 <-> PIN D1/D2
  Arduino <-> ESP
  Switching from UART Communication to
  I2C Communication
  Before: PIN 10/11 <-> PIN D1/D2
  After: PIN A4/A5 <-> PIN D1/D2

custom parts:
  2 channel relay module: 2 channel Relay Module 5V 12V 24V High and Low Level Trigger Relay Control With Optocoupler Two Way relays DC 5 V 12 V 24 V Volt.
  MQ-7 breakout: MP-2 gas sensor
  KY-026: ky-026 flame sensor module
  DHT22 module: DHT22 module. Pins VCC Data GND.
